# Fritzing sketch Untitled Sketch (saved by Fritzing 0.9.3b)

parts:
  U1 = Module 4 Relais 5V [package="Module 4 Relais 5V"]
  U2 = NodeMCU V1.0
  VCC1 = Battery

nets:
  VCC: U1.VCC, U2.Vin
  GND: U1.GND, U1.IN3, U2.GND, U2.D5, VCC1.-
  N1: U1.IN1, U2.D0, U2.D1
  N2: U1.IN2, U2.D2
  N3: U1.IN4, U2.D6

custom parts:
  Module 4 Relais 5V: Module 4 Relais 5V 4x SPD-06VDC-SD-C
  NodeMCU V1.0: ESP8266 based NodeMCU
