# Fritzing sketch Untitled Sketch (saved by Fritzing 0.9.3b)

parts:
  Part1 = Arduino Uno (Rev3) - ICSP
  S1 = H-Bridge with L298N
  M1 = DC Motor
  M2 = DC Motor
  M3 = DC Motor
  M4 = DC Motor
  Mod1 = HC-SR04 Ultrasonic Distance Sensor
  VCC1 = 4 x AAA Battery Mount
  J1 = Basic Servo

nets:
  N1: Part1.A1, Mod1.TRIG
  N2: Part1.A2, Mod1.ECHO
  N3: Part1.D4, S1.IN4
  N4: Part1.D5_PWM, S1.IN3
  N5: Part1.D6_PWM, S1.IN2
  N6: Part1.D7, S1.IN1
  3V3: Part1.3V3, J1.vcc
  5V: Part1.5V, Mod1.VCC
  GND: Part1.GND, S1.GND, Mod1.GND, VCC1.-, J1.gnd
  VIN: Part1.VIN, S1.5V
  N7: S1.12V, VCC1.+
  N8: S1.M1-01, M1.pin_2, M3.pin_2
  N9: S1.M1-02, M1.pin_1
  N10: S1.M2-01, M2.pin_2, M4.pin_2
  N11: S1.M2-02, M2.pin_1, M4.pin_1

custom parts:
  H-Bridge with L298N: h-bridge
  HC-SR04 Ultrasonic Distance Sensor: The HC-SR04 is an ultrasonic distance sensor. It is capable of providing measurement for ranges of 2cm to 400cm. The module operates at 5V.
