# Fritzing sketch bluetooth rc car (saved by Fritzing 0.9.3b)

parts:
  Part1 = Arduino Uno (Rev3) - ICSP
  Part2 = Bluetooth HC-05 Macho
  S1 = H-Bridge with L298N
  M1 = DC Motor
  M2 = DC Motor
  M3 = DC Motor
  M4 = DC Motor
  VCC1 = 4 x AAA Battery Mount

nets:
  N1: Part1.D0/RX, Part2.TXD
  N2: Part1.D1/TX, Part2.RXD
  N3: Part1.D4, S1.IN4
  N4: Part1.D5_PWM, S1.IN3
  N5: Part1.D6_PWM, S1.IN2
  N6: Part1.D7, S1.IN1
  3V3: Part1.3V3, Part2.VCC
  GND: Part1.GND, Part2.GND, S1.GND, VCC1.-
  VIN: Part1.VIN, S1.5V
  N7: S1.12V, VCC1.+
  N8: S1.M1-01, M1.pin_2, M2.pin_2
  N9: S1.M1-02, M1.pin_1, M2.pin_1
  N10: S1.M2-01, M3.pin_2, M4.pin_2
  N11: S1.M2-02, M3.pin_1, M4.pin_1

custom parts:
  H-Bridge with L298N: h-bridge
