# Fritzing sketch bluetooth rc car (saved by Fritzing 0.9.3b)

parts:
  Part1 = Arduino Uno (Rev3) - ICSP
  Part2 = Bluetooth HC-05 Macho
  S1 = H-Bridge with L298N
  M1 = DC Motor
  M2 = DC Motor
  M3 = DC Motor
  M4 = DC Motor
  VCC1 = 4 x AAA Battery Mount
  J1 = Piezo Speaker
  LED1 = LED - 3mm [color="Red (633nm)" package="3 mm [THT]"]
  LED2 = LED - 3mm [color="Red (633nm)" package="3 mm [THT]"]
  LED3 = LED - 3mm [color="Red (633nm)" package="3 mm [THT]"]

nets:
  N1: Part1.D8, J1.pin1
  N2: Part1.D9_PWM, S1.IN2
  N3: Part1.D10_PWM/SS, S1.IN1
  N4: Part1.D11_PWM/MOSI, LED1.cathode
  N5: Part1.D12/MISO, LED2.cathode
  N6: Part1.D13/SCK, LED3.cathode
  N7: Part1.D0/RX, Part2.TXD
  N8: Part1.D1/TX, Part2.RXD
  N9: Part1.D4, S1.IN4
  N10: Part1.D5_PWM, S1.IN3
  N11: Part1.3V3, J1.pin2, LED1.anode, LED2.anode, LED3.anode
  5V: Part1.5V, Part2.VCC
  GND: Part1.GND, Part2.GND, S1.GND, VCC1.-
  VIN: Part1.VIN, S1.5V
  N12: S1.12V, VCC1.+
  N13: S1.M1-01, M1.pin_2, M2.pin_2
  N14: S1.M1-02, M1.pin_1, M2.pin_1
  N15: S1.M2-01, M3.pin_2, M4.pin_2
  N16: S1.M2-02, M3.pin_1, M4.pin_1

custom parts:
  H-Bridge with L298N: h-bridge
